# Fritzing sketch wiring (saved by Fritzing 0.7.1b)
breadboards: 1

parts:
  U1 = Optocoupler [package=THT]
  U2 = Optocoupler [package=THT]
  S1 = Pushbutton [package="[THT]"]
  R1 = Resistor [tolerance=±5% resistance=220 package=THT]
  Arduino1 = Arduino
  R2 = Resistor [tolerance=±5% resistance=220 package=THT]
  S2 = Pushbutton [package="[THT]"]
  R3 = Resistor [tolerance=±5% resistance=33k package=THT]
  R4 = Resistor [tolerance=±5% resistance=3.3k package=THT]
  R5 = Resistor [tolerance=±5% resistance=2.2k package=THT]
  S3 = Pushbutton [package="[THT]"]
  R6 = Resistor [tolerance=±5% resistance=220 package=THT]
  R7 = Resistor [tolerance=±5% resistance=220 package=THT]
  LED1 = LED - 5mm [color="Green (555nm)" package="5 mm [THT]"]
  LED2 = LED - 5mm [color="Red (633nm)" package="5 mm [THT]"]

nets (from the schematic view):
  N1: U1.Pin_1, R1.Pin_0
  N2: U1.Pin_2, U2.Pin_2, Arduino1.GND, S3.Pin_1, S3.Pin_2, LED1.cathode, LED2.cathode
  N3: U1.Pin_4, U2.Pin_4, S1.Pin_1, S1.Pin_2, S2.Pin_1, S2.Pin_2, R3.Pin_0
  N4: U1.Pin_5, S1.Pin_3, S1.Pin_4, R4.Pin_0, R5.Pin_0
  N5: U2.Pin_1, R2.Pin_1
  N6: U2.Pin_5, S2.Pin_3, S2.Pin_4, R3.Pin_1, R4.Pin_1
  N7: R1.Pin_1, Arduino1.D8
  N8: Arduino1.D7, R2.Pin_0
  N9: Arduino1.D3, R6.Pin_0
  N10: Arduino1.D2, R7.Pin_0
  N11: Arduino1.D0RX, S3.Pin_3, S3.Pin_4
  N12: R6.Pin_1, LED1.anode
  N13: R7.Pin_1, LED2.anode
